// Logisim project cpuT_22inst.circ as structural Verilog: 6 circuits, main circuit main
module main (
  input  Clear,
  input  RegW_En
);

  wire clock_1_out, Control_Logic_alu_on, Control_Logic_alu_sel;
  wire [4:0] Control_Logic_alucmd_sel;
  wire [31:0] ALU_alu_out, IMEM_instruction, IMEM_pc, Imm_Gen_imm_out, multiplexer_1_out, reg_file_1_rs1data,
       reg_file_1_rs2data;

  IMEM IMEM (.PC(IMEM_pc), .Instruction(IMEM_instruction));
  Control_Logic Control_Logic (
    .Instruction(IMEM_instruction), .ALUCmd_sel(Control_Logic_alucmd_sel), .ALU_on(Control_Logic_alu_on),
    .ALU_sel(Control_Logic_alu_sel));
  Reg_File reg_file_1 (
    .Rs1(IMEM_instruction[19:15]), .Rs2(IMEM_instruction[24:20]), .Rd(IMEM_instruction[11:7]),
    .RegW_En(RegW_En), .Clear(Clear), .WData(ALU_alu_out), .Rs1Data(reg_file_1_rs1data),
    .Rs2Data(reg_file_1_rs2data));
  Imm_Gen Imm_Gen (.Instruction(IMEM_instruction), .Imm_out(Imm_Gen_imm_out));
  ALU ALU (
    .PC(IMEM_pc), .A(reg_file_1_rs1data), .B(multiplexer_1_out), .ALUCmd_sel(Control_Logic_alucmd_sel),
    .ALU_sel(Control_Logic_alu_sel), .ALU_out(ALU_alu_out));
  Multiplexer #(.width(32), .enable("false")) multiplexer_1 (
    .in0(Imm_Gen_imm_out), .in1(reg_file_1_rs2data), .out(multiplexer_1_out), .sel(IMEM_instruction[5]));
  Clock clock_1 (.out(clock_1_out));

  // Notes on the sheet:
  //   Instruction
  //   PC
  //   Rs1
  //   Rs2
  //   Rd
  //   Clear
  //   RegW_En
  //   WData
  //   Rs1Data
  //   ALU-sel
  //   Rs2Data
  //   Reg_File
  //   Imm-out
  //   ALU-out
  //   ALUCmd-sel
endmodule

module Reg_File (
  input  [4:0] Rs1,
  input  [4:0] Rs2,
  input  [31:0] WData,
  input  [4:0] Rd,
  input  RegW_En,
  input  Clear,
  output [31:0] Rs1Data,
  output [31:0] Rs2Data
);

  wire clock_1_out, decoder_1_out0, decoder_1_out1, decoder_2_out0, decoder_2_out1, decoder_2_out2,
       decoder_2_out3, decoder_3_out0, decoder_3_out1, decoder_3_out2, decoder_3_out3, decoder_4_out0,
       decoder_4_out1, decoder_4_out2, decoder_4_out3, decoder_5_out0, decoder_5_out1, decoder_5_out2,
       decoder_5_out3, decoder_6_out0, decoder_6_out1, decoder_6_out2, decoder_6_out3, decoder_7_out0,
       decoder_7_out1, decoder_7_out2, decoder_7_out3, decoder_8_out0, decoder_8_out1, decoder_8_out2,
       decoder_8_out3, decoder_9_out0, decoder_9_out1, decoder_9_out2, decoder_9_out3, decoder_10_out0,
       decoder_10_out1, decoder_10_out2, decoder_10_out3, decoder_11_out0, decoder_11_out1, decoder_11_out2,
       decoder_11_out3;
  wire [31:0] multiplexer_1_out, multiplexer_2_out, multiplexer_3_out, multiplexer_4_out, multiplexer_5_out,
       multiplexer_6_out, multiplexer_7_out, multiplexer_8_out, multiplexer_9_out, multiplexer_10_out,
       multiplexer_13_out, multiplexer_14_out, multiplexer_15_out, multiplexer_16_out, multiplexer_17_out,
       multiplexer_18_out, multiplexer_19_out, multiplexer_20_out, multiplexer_21_out, multiplexer_22_out,
       x0_q, x1_q, x2_q, x3_q, x4_q, x5_q, x6_q, x7_q, x8_q, x9_q, x10_q, x11_q, x12_q, x13_q, x14_q, x15_q,
       x16_q, x17_q, x18_q, x19_q, x20_q, x21_q, x22_q, x23_q, x24_q, x25_q, x26_q, x27_q, x28_q, x29_q,
       x30_q, x31_q;

  Decoder #(.disabled(0)) decoder_1 (.out0(decoder_1_out0), .out1(decoder_1_out1), .sel(Rd[4]), .en(RegW_En));
  Clock clock_1 (.out(clock_1_out));
  Decoder #(.select(2), .disabled(0)) decoder_2 (
    .out0(decoder_2_out0), .out1(decoder_2_out1), .out2(decoder_2_out2), .out3(decoder_2_out3),
    .sel(Rd[3:2]), .en(decoder_1_out0));
  Decoder #(.select(2), .disabled(0)) decoder_3 (
    .out0(decoder_3_out0), .out1(decoder_3_out1), .out2(decoder_3_out2), .out3(decoder_3_out3),
    .sel(Rd[1:0]), .en(decoder_2_out0));
  Decoder #(.select(2), .disabled(0)) decoder_4 (
    .out0(decoder_4_out0), .out1(decoder_4_out1), .out2(decoder_4_out2), .out3(decoder_4_out3),
    .sel(Rd[1:0]), .en(decoder_2_out1));
  Decoder #(.select(2), .disabled(0)) decoder_5 (
    .out0(decoder_5_out0), .out1(decoder_5_out1), .out2(decoder_5_out2), .out3(decoder_5_out3),
    .sel(Rd[1:0]), .en(decoder_2_out2));
  Decoder #(.select(2), .disabled(0)) decoder_6 (
    .out0(decoder_6_out0), .out1(decoder_6_out1), .out2(decoder_6_out2), .out3(decoder_6_out3),
    .sel(Rd[1:0]), .en(decoder_2_out3));
  Register #(.width(32)) x0 (.D({32{1'b0}}), .en(decoder_3_out0), .Q(x0_q), .clk(clock_1_out), .clr(Clear));
  Register #(.width(32)) x1 (.D(WData), .en(decoder_3_out1), .Q(x1_q), .clk(clock_1_out), .clr(Clear));
  Register #(.width(32)) x2 (.D(WData), .en(decoder_3_out2), .Q(x2_q), .clk(clock_1_out), .clr(Clear));
  Register #(.width(32)) x3 (.D(WData), .en(decoder_3_out3), .Q(x3_q), .clk(clock_1_out), .clr(Clear));
  Register #(.width(32)) x4 (.D(WData), .en(decoder_4_out0), .Q(x4_q), .clk(clock_1_out), .clr(Clear));
  Register #(.width(32)) x5 (.D(WData), .en(decoder_4_out1), .Q(x5_q), .clk(clock_1_out), .clr(Clear));
  Register #(.width(32)) x6 (.D(WData), .en(decoder_4_out2), .Q(x6_q), .clk(clock_1_out), .clr(Clear));
  Register #(.width(32)) x7 (.D(WData), .en(decoder_4_out3), .Q(x7_q), .clk(clock_1_out), .clr(Clear));
  Register #(.width(32)) x8 (.D(WData), .en(decoder_5_out0), .Q(x8_q), .clk(clock_1_out), .clr(Clear));
  Register #(.width(32)) x9 (.D(WData), .en(decoder_5_out1), .Q(x9_q), .clk(clock_1_out), .clr(Clear));
  Register #(.width(32)) x10 (.D(WData), .en(decoder_5_out2), .Q(x10_q), .clk(clock_1_out), .clr(Clear));
  Register #(.width(32)) x11 (.D(WData), .en(decoder_5_out3), .Q(x11_q), .clk(clock_1_out), .clr(Clear));
  Register #(.width(32)) x12 (.D(WData), .en(decoder_6_out0), .Q(x12_q), .clk(clock_1_out), .clr(Clear));
  Register #(.width(32)) x13 (.D(WData), .en(decoder_6_out1), .Q(x13_q), .clk(clock_1_out), .clr(Clear));
  Register #(.width(32)) x14 (.D(WData), .en(decoder_6_out2), .Q(x14_q), .clk(clock_1_out), .clr(Clear));
  Register #(.width(32)) x15 (.D(WData), .en(decoder_6_out3), .Q(x15_q), .clk(clock_1_out), .clr(Clear));
  Multiplexer #(.select(2), .width(32), .disabled(0)) multiplexer_1 (
    .in0(x0_q), .in1(x1_q), .in2(x2_q), .in3(x3_q), .out(multiplexer_1_out), .sel(Rs1[1:0]), .en(1'b1));
  Multiplexer #(.select(2), .width(32), .disabled(0)) multiplexer_2 (
    .in0(x4_q), .in1(x5_q), .in2(x6_q), .in3(x7_q), .out(multiplexer_2_out), .sel(Rs1[1:0]), .en(1'b1));
  Multiplexer #(.select(2), .width(32), .disabled(0)) multiplexer_3 (
    .in0(x8_q), .in1(x9_q), .in2(x10_q), .in3(x11_q), .out(multiplexer_3_out), .sel(Rs1[1:0]), .en(1'b1));
  Multiplexer #(.select(2), .width(32), .disabled(0)) multiplexer_4 (
    .in0(x12_q), .in1(x13_q), .in2(x14_q), .in3(x15_q), .out(multiplexer_4_out), .sel(Rs1[1:0]), .en(1'b1));
  Multiplexer #(.select(2), .width(32), .disabled(0)) multiplexer_5 (
    .in0(x0_q), .in1(x1_q), .in2(x2_q), .in3(x3_q), .out(multiplexer_5_out), .sel(Rs2[1:0]), .en(1'b1));
  Multiplexer #(.select(2), .width(32), .disabled(0)) multiplexer_6 (
    .in0(x4_q), .in1(x5_q), .in2(x6_q), .in3(x7_q), .out(multiplexer_6_out), .sel(Rs2[1:0]), .en(1'b1));
  Multiplexer #(.select(2), .width(32), .disabled(0)) multiplexer_7 (
    .in0(x8_q), .in1(x9_q), .in2(x10_q), .in3(x11_q), .out(multiplexer_7_out), .sel(Rs2[1:0]), .en(1'b1));
  Multiplexer #(.select(2), .width(32), .disabled(0)) multiplexer_8 (
    .in0(x12_q), .in1(x13_q), .in2(x14_q), .in3(x15_q), .out(multiplexer_8_out), .sel(Rs2[1:0]), .en(1'b1));
  Multiplexer #(.select(2), .width(32), .disabled(0)) multiplexer_9 (
    .in0(multiplexer_1_out), .in1(multiplexer_2_out), .in2(multiplexer_3_out), .in3(multiplexer_4_out),
    .out(multiplexer_9_out), .sel(Rs1[3:2]), .en(1'b1));
  Multiplexer #(.select(2), .width(32), .disabled(0)) multiplexer_10 (
    .in0(multiplexer_5_out), .in1(multiplexer_6_out), .in2(multiplexer_7_out), .in3(multiplexer_8_out),
    .out(multiplexer_10_out), .sel(Rs2[3:2]), .en(1'b1));
  Decoder #(.select(2), .disabled(0)) decoder_7 (
    .out0(decoder_7_out0), .out1(decoder_7_out1), .out2(decoder_7_out2), .out3(decoder_7_out3),
    .sel(Rd[3:2]), .en(decoder_1_out1));
  Multiplexer #(.width(32), .disabled(0)) multiplexer_11 (
    .in0(multiplexer_9_out), .in1(multiplexer_21_out), .out(Rs1Data), .sel(Rs1[4]), .en(1'b1));
  Multiplexer #(.width(32), .disabled(0)) multiplexer_12 (
    .in0(multiplexer_10_out), .in1(multiplexer_22_out), .out(Rs2Data), .sel(Rs2[4]), .en(1'b1));
  Decoder #(.select(2), .disabled(0)) decoder_8 (
    .out0(decoder_8_out0), .out1(decoder_8_out1), .out2(decoder_8_out2), .out3(decoder_8_out3),
    .sel(Rd[1:0]), .en(decoder_7_out0));
  Decoder #(.select(2), .disabled(0)) decoder_9 (
    .out0(decoder_9_out0), .out1(decoder_9_out1), .out2(decoder_9_out2), .out3(decoder_9_out3),
    .sel(Rd[1:0]), .en(decoder_7_out1));
  Decoder #(.select(2), .disabled(0)) decoder_10 (
    .out0(decoder_10_out0), .out1(decoder_10_out1), .out2(decoder_10_out2), .out3(decoder_10_out3),
    .sel(Rd[1:0]), .en(decoder_7_out2));
  Decoder #(.select(2), .disabled(0)) decoder_11 (
    .out0(decoder_11_out0), .out1(decoder_11_out1), .out2(decoder_11_out2), .out3(decoder_11_out3),
    .sel(Rd[1:0]), .en(decoder_7_out3));
  Register #(.width(32)) x16 (.D(WData), .en(decoder_8_out0), .Q(x16_q), .clk(clock_1_out), .clr(Clear));
  Register #(.width(32)) x17 (.D(WData), .en(decoder_8_out1), .Q(x17_q), .clk(clock_1_out), .clr(Clear));
  Register #(.width(32)) x18 (.D(WData), .en(decoder_8_out2), .Q(x18_q), .clk(clock_1_out), .clr(Clear));
  Register #(.width(32)) x19 (.D(WData), .en(decoder_8_out3), .Q(x19_q), .clk(clock_1_out), .clr(Clear));
  Register #(.width(32)) x20 (.D(WData), .en(decoder_9_out0), .Q(x20_q), .clk(clock_1_out), .clr(Clear));
  Register #(.width(32)) x21 (.D(WData), .en(decoder_9_out1), .Q(x21_q), .clk(clock_1_out), .clr(Clear));
  Register #(.width(32)) x22 (.D(WData), .en(decoder_9_out2), .Q(x22_q), .clk(clock_1_out), .clr(Clear));
  Register #(.width(32)) x23 (.D(WData), .en(decoder_9_out3), .Q(x23_q), .clk(clock_1_out), .clr(Clear));
  Register #(.width(32)) x24 (.D(WData), .en(decoder_10_out0), .Q(x24_q), .clk(clock_1_out), .clr(Clear));
  Register #(.width(32)) x25 (.D(WData), .en(decoder_10_out1), .Q(x25_q), .clk(clock_1_out), .clr(Clear));
  Register #(.width(32)) x26 (.D(WData), .en(decoder_10_out2), .Q(x26_q), .clk(clock_1_out), .clr(Clear));
  Register #(.width(32)) x27 (.D(WData), .en(decoder_10_out3), .Q(x27_q), .clk(clock_1_out), .clr(Clear));
  Register #(.width(32)) x28 (.D(WData), .en(decoder_11_out0), .Q(x28_q), .clk(clock_1_out), .clr(Clear));
  Register #(.width(32)) x29 (.D(WData), .en(decoder_11_out1), .Q(x29_q), .clk(clock_1_out), .clr(Clear));
  Register #(.width(32)) x30 (.D(WData), .en(decoder_11_out2), .Q(x30_q), .clk(clock_1_out), .clr(Clear));
  Register #(.width(32)) x31 (.D(WData), .en(decoder_11_out3), .Q(x31_q), .clk(clock_1_out), .clr(Clear));
  Register #(.width(32)) register_1 (.clk(clock_1_out));  // open: D, en, Q, clr
  Register #(.width(32)) register_2 (.clk(clock_1_out));  // open: D, en, Q, clr
  Multiplexer #(.select(2), .width(32), .disabled(0)) multiplexer_13 (
    .in0(x16_q), .in1(x17_q), .in2(x18_q), .in3(x19_q), .out(multiplexer_13_out), .sel(Rs1[1:0]), .en(1'b1));
  Multiplexer #(.select(2), .width(32), .disabled(0)) multiplexer_14 (
    .in0(x20_q), .in1(x21_q), .in2(x22_q), .in3(x23_q), .out(multiplexer_14_out), .sel(Rs1[1:0]), .en(1'b1));
  Multiplexer #(.select(2), .width(32), .disabled(0)) multiplexer_15 (
    .in0(x24_q), .in1(x25_q), .in2(x26_q), .in3(x27_q), .out(multiplexer_15_out), .sel(Rs1[1:0]), .en(1'b1));
  Multiplexer #(.select(2), .width(32), .disabled(0)) multiplexer_16 (
    .in0(x28_q), .in1(x29_q), .in2(x30_q), .in3(x31_q), .out(multiplexer_16_out), .sel(Rs1[1:0]), .en(1'b1));
  Multiplexer #(.select(2), .width(32), .disabled(0)) multiplexer_17 (
    .in0(x16_q), .in1(x17_q), .in2(x18_q), .in3(x19_q), .out(multiplexer_17_out), .sel(Rs2[1:0]), .en(1'b1));
  Multiplexer #(.select(2), .width(32), .disabled(0)) multiplexer_18 (
    .in0(x20_q), .in1(x21_q), .in2(x22_q), .in3(x23_q), .out(multiplexer_18_out), .sel(Rs2[1:0]), .en(1'b1));
  Multiplexer #(.select(2), .width(32), .disabled(0)) multiplexer_19 (
    .in0(x24_q), .in1(x25_q), .in2(x26_q), .in3(x27_q), .out(multiplexer_19_out), .sel(Rs2[1:0]), .en(1'b1));
  Multiplexer #(.select(2), .width(32), .disabled(0)) multiplexer_20 (
    .in0(x28_q), .in1(x29_q), .in2(x30_q), .in3(x31_q), .out(multiplexer_20_out), .sel(Rs2[1:0]), .en(1'b1));
  Multiplexer #(.select(2), .width(32)) multiplexer_21 (
    .in0(multiplexer_13_out), .in1(multiplexer_14_out), .in2(multiplexer_15_out), .in3(multiplexer_16_out),
    .out(multiplexer_21_out), .sel(Rs1[3:2]), .en(1'b1));
  Multiplexer #(.select(2), .width(32)) multiplexer_22 (
    .in0(multiplexer_17_out), .in1(multiplexer_18_out), .in2(multiplexer_19_out), .in3(multiplexer_20_out),
    .out(multiplexer_22_out), .sel(Rs2[3:2]), .en(1'b1));

  // Notes on the sheet:
  //   for Reg 1
  //   for Reg 2
  //   for Reg 1
  //   for Reg 2
endmodule

module ALU (
  input  [31:0] PC,
  input  [31:0] A,
  input  ALU_sel,
  input  [31:0] B,
  input  [4:0] ALUCmd_sel,
  output [31:0] ALU_out
);

  wire comparator_1_lt, comparator_2_lt, comparator_3_lt, comparator_4_lt;
  wire [4:0] bit_extender_1_out, bit_extender_2_out, bit_extender_3_out, bit_extender_4_out,
       bit_extender_5_out, bit_extender_6_out;
  wire [31:0] adder_1_out, adder_2_out, adder_3_out, adder_4_out, and_1_out, and_2_out, bit_extender_7_out,
       bit_extender_8_out, bit_extender_9_out, bit_extender_10_out, divider_2_out, divider_4_rem,
       multiplier_1_out, multiplier_2_out, negator_1_out, or_1_out, or_2_out, shifter_1_out, shifter_2_out,
       shifter_3_out, shifter_4_out, shifter_5_out, shifter_6_out, shifter_7_out, shifter_8_out, undriven,
       undriven_2, undriven_3, undriven_4, undriven_5, undriven_6, undriven_7, undriven_8, undriven_9,
       XOR_2_out, XOR_out;

  Negator #(.width(32)) negator_1 (.in(B), .out(negator_1_out));
  Comparator #(.width(32)) comparator_1 (.a(A), .b(B), .lt(comparator_1_lt));  // open: gt, eq
  Comparator #(.width(32)) comparator_2 (.a(A), .b(B), .lt(comparator_2_lt));  // open: gt, eq
  Comparator #(.width(32), .mode("unsigned")) comparator_3 (.a(A), .b(B), .lt(comparator_3_lt));  // open: gt, eq
  Comparator #(.width(32), .mode("unsigned")) comparator_4 (.a(A), .b(B), .lt(comparator_4_lt));  // open: gt, eq
  Bit_Extender #(.in_width(32), .out_width(5)) bit_extender_1 (.in(B), .out(bit_extender_1_out));
  Bit_Extender #(.in_width(32), .out_width(5)) bit_extender_2 (.in(B), .out(bit_extender_2_out));
  Bit_Extender #(.in_width(32), .out_width(5)) bit_extender_3 (.in(B), .out(bit_extender_3_out));
  Bit_Extender #(.in_width(32), .out_width(5)) bit_extender_4 (.in(B), .out(bit_extender_4_out));
  Bit_Extender #(.in_width(32), .out_width(5)) bit_extender_5 (.in(B), .out(bit_extender_5_out));
  Bit_Extender #(.in_width(32), .out_width(5)) bit_extender_6 (.in(B), .out(bit_extender_6_out));
  assign XOR_out = A ^ B;  // XOR_Gate XOR, 32 bits wide
  assign XOR_2_out = A ^ B;  // XOR_Gate XOR_2, 32 bits wide
  assign or_1_out = A | B;  // OR_Gate or_1, 32 bits wide
  assign or_2_out = A | B;  // OR_Gate or_2, 32 bits wide
  assign and_1_out = A & B;  // AND_Gate and_1, 32 bits wide
  assign and_2_out = A & B;  // AND_Gate and_2, 32 bits wide
  Adder #(.width(32)) adder_1 (.a(A), .b(B), .out(adder_1_out));  // open: cin, cout
  Adder #(.width(32)) adder_2 (.a(A), .b(B), .out(adder_2_out));  // open: cin, cout
  Adder #(.width(32)) adder_3 (.a(A), .b(negator_1_out), .out(adder_3_out));  // open: cin, cout
  Shifter #(.width(32)) shifter_1 (.in(undriven), .\dist (5'b01100), .out(shifter_1_out));
  Adder #(.width(32)) adder_4 (.a(PC), .b(shifter_2_out), .out(adder_4_out));  // open: cin, cout
  Shifter #(.width(32)) shifter_2 (.in(undriven_2), .\dist (5'b01100), .out(shifter_2_out));
  assign bit_extender_7_out = {{31{1'b0}}, comparator_1_lt};  // Bit_Extender bit_extender_7
  assign bit_extender_8_out = {{31{1'b0}}, comparator_2_lt};  // Bit_Extender bit_extender_8
  assign bit_extender_9_out = {{31{1'b0}}, comparator_3_lt};  // Bit_Extender bit_extender_9
  assign bit_extender_10_out = {{31{1'b0}}, comparator_4_lt};  // Bit_Extender bit_extender_10
  Shifter #(.width(32)) shifter_3 (.in(A), .\dist (bit_extender_1_out), .out(shifter_3_out));
  Shifter #(.width(32)) shifter_4 (.in(A), .\dist (bit_extender_2_out), .out(shifter_4_out));
  Shifter #(.width(32), .shift("lr")) shifter_5 (.in(A), .\dist (bit_extender_3_out), .out(shifter_5_out));
  Shifter #(.width(32), .shift("lr")) shifter_6 (.in(A), .\dist (bit_extender_4_out), .out(shifter_6_out));
  Shifter #(.width(32), .shift("ar")) shifter_7 (.in(A), .\dist (bit_extender_5_out), .out(shifter_7_out));
  Shifter #(.width(32), .shift("ar")) shifter_8 (.in(A), .\dist (bit_extender_6_out), .out(shifter_8_out));
  Multiplier #(.width(32)) multiplier_1 (.a(A), .b(B), .out(multiplier_1_out));  // open: cin, cout
  Shifter #(.width(32), .shift("lr")) shifter_9 (.in(multiplier_2_out), .\dist ({5{1'b0}}));  // open: out
  Multiplier #(.width(32)) multiplier_2 (.out(multiplier_2_out));  // open: a, b, cin, cout
  Multiplier #(.width(32)) multiplier_3 ();  // open: a, b, out, cin, cout
  Multiplier #(.width(32)) multiplier_4 ();  // open: a, b, out, cin, cout
  Divider #(.width(32)) divider_1 (.a(undriven_3), .b(undriven_4));  // open: out, upper, rem
  Divider #(.width(32)) divider_2 (.a(A), .b(B), .out(divider_2_out));  // open: upper, rem
  Divider #(.width(32)) divider_3 ();  // open: a, b, out, upper, rem
  Divider #(.width(32)) divider_4 (.a(A), .b(B), .rem(divider_4_rem));  // open: out, upper
  Multiplexer #(.select(5), .width(32)) multiplexer_1 (
    .in1(adder_1_out), .in2(adder_2_out), .in3(adder_3_out), .in6(bit_extender_7_out),
    .in7(bit_extender_8_out), .in8(bit_extender_9_out), .in9(bit_extender_10_out), .in10(shifter_3_out),
    .in11(shifter_4_out), .in12(shifter_5_out), .in13(shifter_6_out), .in14(shifter_7_out),
    .in15(shifter_8_out), .in16(XOR_out), .in17(XOR_2_out), .in18(or_1_out), .in19(or_2_out),
    .in20(and_1_out), .in21(and_2_out), .in22(multiplier_1_out), .in23(undriven_6), .in24(undriven_7),
    .in25(undriven_8), .in26(undriven_9), .in27(divider_2_out), .in28(undriven_5), .in29(divider_4_rem),
    .out(ALU_out), .sel(ALUCmd_sel), .en(ALU_sel));  // open: in0, in4, in5, in30, in31

  // Notes on the sheet:
  //   B
  //   A
  //   B
  //   6 SLT
  //   7 SLTI
  //   16 XOR
  //   17 XORI
  //   18 OR
  //   19 ORI
  //   20 AND
  //   21 ANDI
  //   22 MUL
  //   24 MULHU
  //   25 MULHSU
  //   27 DIVU
  //   28 REM
  //   29 REMU
  //   1 Add
  //   2 Addi
  //   3 Sub
  //   4 Lui
  //   5 Auipc
  //   8 SLTU
  //   9 SLTIU
  //   10 SLL
  //   11 SLLI
  //   12 SRL
  //   13 SRLI
  //   14 SRA
  //   15 SRAI
  //   23 MULH
  //   26 DIV
  //   Multiplier is doing signed multiplication
  //   and giving lower 32-bits at the output.
  //   Divider is doing unsigned division.
  //   Divider is doing unsigned division.
endmodule

module IMEM (
  output [31:0] PC,
  output [31:0] Instruction
);

  wire clock_1_out;
  wire [31:0] register_1_q;

  Clock clock_1 (.out(clock_1_out));
  Register #(.width(32)) register_1 (.D(PC), .en(1'b1), .Q(register_1_q), .clk(clock_1_out));  // open: clr
  Adder #(.width(32)) adder_1 (.a(32'h4), .b(register_1_q), .out(PC));  // open: cin, cout
  ROM #(.addrWidth(14), .dataWidth(32)) rom_1 (.addr(register_1_q[15:2]), .data(Instruction));  // open: sel

  // Notes on the sheet:
  //   contents of rom_1 (hex, n*v repeats v):
  //   100093 200113 300193 400213 500293 600313 700393 800413 900493 a00513 b00593 c00613 d00693 e00713
  //   f00793 1000813 1100893 1200913 1300993 1400a13 1500a93 1600b13 1700b93 1800c13 1101b3 40428333 193b7
  //   1a417 9525b3 1b62693 e7b833 1c8b913 13a1ab3 5b1b93 180d133 51d213 405353b3 405bd493 a5c633 86c713
  //   f868b3 896993 14afb33 8bfc13 2398233 29253b3 2927533 5*13 100093 200113 300193 400213 500293 600313
  //   700393 800413 900493 a00513 b00593 c00613 d00693 e00713 f00793 1000813 1100893 1200913 1300993
  //   1400a13 1500a93 1600b13 1700b93 1800c13 1101b3 40428333 193b7 1a417 9525b3 1b62693 e7b833 1c8b913
  //   13a1ab3 5b1b93 180d133 51d213 405353b3 405bd493 a5c633 86c713 f868b3 896993 14afb33 8bfc13 2398233
  //   29253b3 2927533 5*13 100093 200113 300193 400213 500293 600313 700393 800413 900493 a00513 b00593
  //   c00613 d00693 e00713 f00793 1000813 1100893 1200913 1300993 1400a13 1500a93 1600b13 1700b93 1800c13
  //   1101b3 40428333 193b7 1a417 9525b3 1b62693 e7b833 1c8b913 13a1ab3 5b1b93 180d133 51d213 405353b3
  //   405bd493 a5c633 86c713 f868b3 896993 14afb33 8bfc13 2398233 29253b3 2927533
endmodule

module Control_Logic (
  input  [31:0] Instruction,
  output [4:0] ALUCmd_sel,
  output ALU_on,
  output ALU_sel
);

  wire and_1_out, decoder_1_out0, decoder_1_out1, decoder_1_out2, decoder_1_out3, decoder_1_out4,
       decoder_1_out5, decoder_1_out6, decoder_1_out7, decoder_1_out8, decoder_1_out9, decoder_1_out10,
       decoder_1_out11, decoder_1_out12, decoder_1_out13, decoder_1_out14, decoder_1_out15, decoder_1_out16,
       decoder_1_out17, decoder_1_out18, decoder_1_out19, decoder_1_out20, decoder_1_out21, decoder_1_out22,
       decoder_1_out23, decoder_1_out24, decoder_1_out25, decoder_1_out26, decoder_1_out27, decoder_1_out28,
       decoder_1_out30, decoder_2_out0, decoder_2_out1, decoder_2_out2, decoder_2_out3, decoder_2_out4,
       decoder_2_out5, decoder_2_out6, decoder_2_out7, demultiplexer_1_out0, demultiplexer_1_out1,
       demultiplexer_2_out0, demultiplexer_2_out1, demultiplexer_3_out0, demultiplexer_3_out1, not_1_out,
       not_2_out, not_3_out, priority_encoder_1_gs;

  and and_1 (and_1_out, Instruction[25], Instruction[5]);
  not not_1 (not_1_out, Instruction[6]);
  not not_2 (not_2_out, Instruction[3]);
  not not_3 (not_3_out, and_1_out);
  and and_2 (ALU_on, not_1_out, Instruction[4], not_2_out, Instruction[1], Instruction[0]);
  Decoder #(.select(5)) decoder_1 (
    .out0(decoder_1_out0), .out1(decoder_1_out1), .out2(decoder_1_out2), .out3(decoder_1_out3),
    .out4(decoder_1_out4), .out5(decoder_1_out5), .out6(decoder_1_out6), .out7(decoder_1_out7),
    .out8(decoder_1_out8), .out9(decoder_1_out9), .out10(decoder_1_out10), .out11(decoder_1_out11),
    .out12(decoder_1_out12), .out13(decoder_1_out13), .out14(decoder_1_out14), .out15(decoder_1_out15),
    .out16(decoder_1_out16), .out17(decoder_1_out17), .out18(decoder_1_out18), .out19(decoder_1_out19),
    .out20(decoder_1_out20), .out21(decoder_1_out21), .out22(decoder_1_out22), .out23(decoder_1_out23),
    .out24(decoder_1_out24), .out25(decoder_1_out25), .out26(decoder_1_out26), .out27(decoder_1_out27),
    .out28(decoder_1_out28), .out30(decoder_1_out30),
    .sel({Instruction[14:12], Instruction[5], Instruction[2]}), .en(not_3_out));  // open: out29, out31
  or or_1 (ALU_sel, Instruction[0], Instruction[1], Instruction[2], Instruction[3], Instruction[4], Instruction[5], Instruction[6], Instruction[7], Instruction[8], Instruction[9], Instruction[10], Instruction[11], Instruction[12], Instruction[13], Instruction[14], Instruction[15], Instruction[16], Instruction[17], Instruction[18], Instruction[19], Instruction[20], Instruction[21], Instruction[22], Instruction[23], Instruction[24], Instruction[25], Instruction[26], Instruction[27], Instruction[28], Instruction[29], Instruction[30], Instruction[31]);
  Decoder #(.select(3)) decoder_2 (
    .out0(decoder_2_out0), .out1(decoder_2_out1), .out2(decoder_2_out2), .out3(decoder_2_out3),
    .out4(decoder_2_out4), .out5(decoder_2_out5), .out6(decoder_2_out6), .out7(decoder_2_out7),
    .sel(Instruction[14:12]), .en(and_1_out));
  Demultiplexer demultiplexer_1 (
    .out0(demultiplexer_1_out0), .out1(demultiplexer_1_out1), .in(decoder_1_out2), .sel(Instruction[30]));  // open: en
  Demultiplexer demultiplexer_2 (
    .out0(demultiplexer_2_out0), .out1(demultiplexer_2_out1), .in(decoder_1_out20), .sel(Instruction[30]));  // open: en
  Demultiplexer demultiplexer_3 (
    .out0(demultiplexer_3_out0), .out1(demultiplexer_3_out1), .in(decoder_1_out22), .sel(Instruction[30]));  // open: en
  Priority_Encoder #(.select(5)) priority_encoder_1 (
    .in1(demultiplexer_1_out0), .in2(decoder_1_out0), .in3(demultiplexer_1_out1), .in4(decoder_1_out7),
    .in5(decoder_1_out9), .in6(decoder_1_out10), .in7(decoder_1_out8), .in8(decoder_1_out14),
    .in9(decoder_1_out12), .in10(decoder_1_out6), .in11(decoder_1_out4), .in12(demultiplexer_3_out0),
    .in13(demultiplexer_2_out0), .in14(demultiplexer_3_out1), .in15(demultiplexer_2_out1),
    .in16(decoder_1_out18), .in17(decoder_1_out16), .in18(decoder_1_out26), .in19(decoder_1_out24),
    .in20(decoder_1_out30), .in21(decoder_1_out28), .in22(decoder_2_out0), .in23(decoder_2_out1),
    .in24(decoder_2_out2), .in25(decoder_2_out3), .in26(decoder_2_out4), .in27(decoder_2_out5),
    .in28(decoder_2_out6), .in29(decoder_2_out7), .out(ALUCmd_sel), .gs(priority_encoder_1_gs), .en_in(1'b1));  // open: in0, in30, in31, en_out

  // Notes on the sheet:
  //   b30
  //   5 auipc
  //   4 Lui
  //   23 MULH
  //   26 DIV
  //   28 REM
  //   17 XORI
  //   13 SRLI
  //   15 SRAI
  //   22 MUL
  //   24 MULHSU
  //   25 MULHU
  //   27 DIVU
  //   29 REMU
  //   10 SLL
  //   9 SLTIU
  //   16 XOR
  //   2 Addi
  //   1 Add
  //   3 Sub
  //   7 SLTI
  //   6 SLT
  //   8 SLTU
  //   12 SRL
  //   14 SRA
  //   18 OR
  //   20 AND
  //   21 ANDI
  //   11 SLLI
  //   19 ORI
endmodule

module Imm_Gen (
  input  [31:0] Instruction,
  output [31:0] Imm_out
);

  assign Imm_out = {{20{Instruction[31]}}, Instruction[31:20]};  // Bit_Extender bit_extender_1
endmodule
