// Logisim project jan29pm-32inst_cpuT.circ as structural Verilog: 8 circuits, main circuit main
module main (
  input  Clear,
  input  RegW_En
);

  wire clock_1_out, control_logic_1_alu_on, control_logic_1_brcond;
  wire [1:0] control_logic_1_jal_r;
  wire [2:2] control_logic_1_alu_sel;
  wire [4:0] control_logic_1_alucmd_sel;
  wire [31:0] adder_1_out, adder_2_out, ALU_alu_out, IMEM_instruction, Imm_Gen_broffset, Imm_Gen_imm_out,
       Imm_Gen_jaloffset, Imm_Gen_uioffset, multiplexer_1_out, multiplexer_2_out, multiplexer_3_out,
       multiplexer_4_out, pc_1_pc_next, reg_file_1_rs1data, reg_file_1_rs2data, shifter_1_out;

  Multiplexer #(.width(32)) multiplexer_1 (
    .in0(32'h4), .in1(Imm_Gen_broffset), .out(multiplexer_1_out), .sel(control_logic_1_brcond));  // open: en
  Multiplexer #(.select(2), .width(32)) multiplexer_2 (
    .in0(multiplexer_1_out), .in1(Imm_Gen_jaloffset), .in2(shifter_1_out), .out(multiplexer_2_out),
    .sel(control_logic_1_jal_r));  // open: in3, en
  Adder #(.width(32)) adder_1 (.a(multiplexer_2_out), .b(pc_1_pc_next), .out(adder_1_out));  // open: cin, cout
  PC pc_1 (.PC_in(adder_1_out), .PC_next(pc_1_pc_next));
  IMEM IMEM (.PC(pc_1_pc_next), .Instruction(IMEM_instruction));
  Clock clock_1 (.out(clock_1_out));
  Control_Logic control_logic_1 (
    .Instruction(IMEM_instruction), .JAL_R(control_logic_1_jal_r), .A(reg_file_1_rs1data),
    .B(multiplexer_3_out), .ALUCmd_sel(control_logic_1_alucmd_sel), .ALU_on(control_logic_1_alu_on),
    .ALU_sel(control_logic_1_alu_sel[2]), .BrCond(control_logic_1_brcond));
  Reg_File reg_file_1 (
    .Rs1(IMEM_instruction[19:15]), .Rs2(IMEM_instruction[24:20]), .Rd(IMEM_instruction[11:7]),
    .RegW_En(RegW_En), .Clear(Clear), .WData(multiplexer_4_out), .Rs1Data(reg_file_1_rs1data),
    .Rs2Data(reg_file_1_rs2data));
  Imm_Gen Imm_Gen (
    .Instruction(IMEM_instruction), .Imm_out(Imm_Gen_imm_out), .BrOffset(Imm_Gen_broffset),
    .jalOffset(Imm_Gen_jaloffset), .uiOffset(Imm_Gen_uioffset));
  Multiplexer #(.width(32), .enable("false")) multiplexer_3 (
    .in0(Imm_Gen_imm_out), .in1(reg_file_1_rs2data), .out(multiplexer_3_out), .sel(IMEM_instruction[5]));
  Adder #(.width(32)) adder_2 (.a(Imm_Gen_imm_out), .b(reg_file_1_rs1data), .out(adder_2_out));  // open: cin, cout
  ALU ALU (
    .PC(pc_1_pc_next), .uiOffset(Imm_Gen_uioffset), .A(reg_file_1_rs1data), .B(multiplexer_3_out),
    .ALUCmd_sel(control_logic_1_alucmd_sel), .ALU_sel(control_logic_1_alu_sel[2]), .ALU_out(ALU_alu_out));
  Shifter #(.width(32)) shifter_1 (.in(adder_2_out), .\dist (5'b00001), .out(shifter_1_out));
  Multiplexer #(.select(3), .width(32)) multiplexer_4 (
    .in1(adder_1_out), .in2(adder_1_out), .in4(ALU_alu_out), .out(multiplexer_4_out),
    .sel({control_logic_1_alu_sel[2], control_logic_1_jal_r}));  // open: in0, in3, in5, in6, in7, en
  DMEM dmem_1 ();  // open: Address, Write_Data, Read_Data

  // Notes on the sheet:
  //   BrCond
  //   JAL/R
  //   JalOffset
  //   BrOffset
  //   JALRoffset
  //   PC+4
  //   Program 
  //   Counter
  //   Instruction
  //   Control_Logic
  //   PC+4
  //   PC
  //   Rs1
  //   Rs2
  //   Rd
  //   Clear
  //   ALU-sel
  //   RegW_En
  //   WData
  //   Rs1Data
  //   Rs2Data
  //   Reg_File
  //   Imm-out
  //   uiOffset
  //   ALUCmd-sel
  //   ALU-out
  //   PC+4
  //   ALU-sel
  //   JALRoffset
  //   JAL/R
  //   WBack
  //   DMEM
endmodule

module PC (
  input  [31:0] PC_in,
  output [31:0] PC_next
);

  wire clock_1_out;

  Clock clock_1 (.out(clock_1_out));
  Register #(.width(32)) register_1 (.D(PC_in), .en(1'b1), .Q(PC_next), .clk(clock_1_out));  // open: clr
endmodule

module IMEM (
  input  [31:0] PC,
  output [31:0] Instruction
);

  ROM #(.addrWidth(14), .dataWidth(32)) rom_1 (.addr(PC[15:2]), .data(Instruction));  // open: sel

  // Notes on the sheet:
  //   contents of rom_1 (hex, n*v repeats v):
  //   100093 200113 300193 400213 500293 600313 700393 800413 900493 a00513 b00593 c00613 d00693 e00713
  //   f00793 1000813 1100893 1200913 1300993 1400a13 1500a93 1600b13 1700b93 1800c13 1900c93 1a00d13
  //   1b00d93 1c00e13 1d00e93 1e00f13 1f00f93 1101b3 40428333 193b7 1a417 9525b3 1b62693 e7b833 1c8b913
  //   13a1ab3 5b1b93 181dcb3 1c0dd13 41b15eb3 4121df13 a5c633 86c713 f868b3 896993 14b7fb3 10ff993 2398233
  //   31253b3 3127533 ff000993 1388463 1389463 100f93 200f93 138d663 138c263 300f13 400f13 138f463 138e463
  //   500f13 600f13 c0006f 700e93 80006f 800e93
endmodule

module Control_Logic (
  input  [31:0] Instruction,
  input  [31:0] A,
  input  [31:0] B,
  output [4:0] ALUCmd_sel,
  output ALU_on,
  output ALU_sel,
  output BrCond,
  output [1:0] JAL_R
);

  wire and_1_out, and_3_out, comparator_1_eq, comparator_2_eq, comparator_3_lt, comparator_4_lt,
       comparator_5_lt, comparator_6_lt, decoder_1_out0, decoder_1_out1, decoder_1_out2, decoder_1_out3,
       decoder_1_out4, decoder_1_out5, decoder_1_out6, decoder_1_out7, decoder_1_out8, decoder_1_out9,
       decoder_1_out10, decoder_1_out11, decoder_1_out12, decoder_1_out13, decoder_1_out14, decoder_1_out15,
       decoder_1_out16, decoder_1_out17, decoder_1_out18, decoder_1_out19, decoder_1_out20, decoder_1_out21,
       decoder_1_out22, decoder_1_out23, decoder_1_out24, decoder_1_out25, decoder_1_out26, decoder_1_out27,
       decoder_1_out28, decoder_1_out30, decoder_2_out0, decoder_2_out1, decoder_2_out2, decoder_2_out3,
       decoder_2_out4, decoder_2_out5, decoder_2_out6, decoder_2_out7, decoder_3_out0, decoder_3_out1,
       decoder_3_out4, decoder_3_out5, decoder_3_out6, decoder_3_out7, demultiplexer_1_out0,
       demultiplexer_1_out1, demultiplexer_2_out0, demultiplexer_2_out1, demultiplexer_3_out0,
       demultiplexer_3_out1, not_1_out, not_2_out, not_3_out, not_4_out, not_5_out, not_6_out, not_7_out,
       not_8_out, or_1_out, priority_encoder_1_gs, priority_encoder_2_gs;
  wire [2:0] priority_encoder_1_out;

  and and_1 (and_1_out, Instruction[25], Instruction[5]);
  not not_1 (not_1_out, Instruction[6]);
  not not_2 (not_2_out, Instruction[3]);
  not not_3 (not_3_out, Instruction[2]);
  not not_4 (not_4_out, Instruction[3]);
  not not_5 (not_5_out, and_1_out);
  and and_2 (ALU_on, not_1_out, Instruction[4], not_2_out, Instruction[1], Instruction[0]);
  Decoder #(.select(5)) decoder_1 (
    .out0(decoder_1_out0), .out1(decoder_1_out1), .out2(decoder_1_out2), .out3(decoder_1_out3),
    .out4(decoder_1_out4), .out5(decoder_1_out5), .out6(decoder_1_out6), .out7(decoder_1_out7),
    .out8(decoder_1_out8), .out9(decoder_1_out9), .out10(decoder_1_out10), .out11(decoder_1_out11),
    .out12(decoder_1_out12), .out13(decoder_1_out13), .out14(decoder_1_out14), .out15(decoder_1_out15),
    .out16(decoder_1_out16), .out17(decoder_1_out17), .out18(decoder_1_out18), .out19(decoder_1_out19),
    .out20(decoder_1_out20), .out21(decoder_1_out21), .out22(decoder_1_out22), .out23(decoder_1_out23),
    .out24(decoder_1_out24), .out25(decoder_1_out25), .out26(decoder_1_out26), .out27(decoder_1_out27),
    .out28(decoder_1_out28), .out30(decoder_1_out30),
    .sel({Instruction[14:12], Instruction[5], Instruction[2]}), .en(not_5_out));  // open: out29, out31
  or or_1 (or_1_out, Instruction[0], Instruction[1], Instruction[2], Instruction[3], Instruction[4], Instruction[5], Instruction[6], Instruction[7], Instruction[8], Instruction[9], Instruction[10], Instruction[11], Instruction[12], Instruction[13], Instruction[14], Instruction[15], Instruction[16], Instruction[17], Instruction[18], Instruction[19], Instruction[20], Instruction[21], Instruction[22], Instruction[23], Instruction[24], Instruction[25], Instruction[26], Instruction[27], Instruction[28], Instruction[29], Instruction[30], Instruction[31]);
  and and_3 (and_3_out, not_3_out, not_4_out, Instruction[6]);
  and and_4 (JAL_R[1], Instruction[2], not_4_out, Instruction[6]);
  and and_5 (JAL_R[0], Instruction[2], Instruction[3], Instruction[6]);
  and and_6 (ALU_sel, ALU_on, or_1_out);
  Decoder #(.select(3)) decoder_2 (
    .out0(decoder_2_out0), .out1(decoder_2_out1), .out2(decoder_2_out2), .out3(decoder_2_out3),
    .out4(decoder_2_out4), .out5(decoder_2_out5), .out6(decoder_2_out6), .out7(decoder_2_out7),
    .sel(Instruction[14:12]), .en(and_1_out));
  Decoder #(.select(3)) decoder_3 (
    .out0(decoder_3_out0), .out1(decoder_3_out1), .out4(decoder_3_out4), .out5(decoder_3_out5),
    .out6(decoder_3_out6), .out7(decoder_3_out7), .sel(Instruction[14:12]), .en(and_3_out));  // open: out2, out3
  Priority_Encoder priority_encoder_1 (
    .in0(decoder_3_out0), .in1(decoder_3_out1), .in4(decoder_3_out4), .in5(decoder_3_out5),
    .in6(decoder_3_out6), .in7(decoder_3_out7), .out(priority_encoder_1_out), .en_in(1'b1),
    .gs(priority_encoder_1_gs));  // open: in2, in3, en_out
  Demultiplexer demultiplexer_1 (
    .out0(demultiplexer_1_out0), .out1(demultiplexer_1_out1), .in(decoder_1_out2), .sel(Instruction[30]));  // open: en
  Demultiplexer demultiplexer_2 (
    .out0(demultiplexer_2_out0), .out1(demultiplexer_2_out1), .in(decoder_1_out20), .sel(Instruction[30]));  // open: en
  Demultiplexer demultiplexer_3 (
    .out0(demultiplexer_3_out0), .out1(demultiplexer_3_out1), .in(decoder_1_out22), .sel(Instruction[30]));  // open: en
  Comparator #(.width(32)) comparator_1 (.a(A), .b(B), .eq(comparator_1_eq));  // open: gt, lt
  Comparator #(.width(32)) comparator_2 (.a(A), .b(B), .eq(comparator_2_eq));  // open: gt, lt
  not not_6 (not_6_out, comparator_2_eq);
  Comparator #(.width(32)) comparator_3 (.a(A), .b(B), .lt(comparator_3_lt));  // open: gt, eq
  Comparator #(.width(32)) comparator_4 (.a(A), .b(B), .lt(comparator_4_lt));  // open: gt, eq
  Comparator #(.width(32), .mode("unsigned")) comparator_5 (.a(A), .b(B), .lt(comparator_5_lt));  // open: gt, eq
  Comparator #(.width(32), .mode("unsigned")) comparator_6 (.a(A), .b(B), .lt(comparator_6_lt));  // open: gt, eq
  not not_7 (not_7_out, comparator_4_lt);
  not not_8 (not_8_out, comparator_6_lt);
  Multiplexer #(.select(3), .disabled(0)) multiplexer_1 (
    .in0(comparator_1_eq), .in1(not_6_out), .in4(comparator_3_lt), .in5(not_7_out), .in6(comparator_5_lt),
    .in7(not_8_out), .out(BrCond), .sel(priority_encoder_1_out), .en(and_3_out));  // open: in2, in3
  Priority_Encoder #(.select(5)) priority_encoder_2 (
    .in1(demultiplexer_1_out0), .in2(decoder_1_out0), .in3(demultiplexer_1_out1), .in4(decoder_1_out7),
    .in5(decoder_1_out9), .in6(decoder_1_out10), .in7(decoder_1_out8), .in8(decoder_1_out14),
    .in9(decoder_1_out12), .in10(decoder_1_out6), .in11(decoder_1_out4), .in12(demultiplexer_3_out0),
    .in13(demultiplexer_2_out0), .in14(demultiplexer_3_out1), .in15(demultiplexer_2_out1),
    .in16(decoder_1_out18), .in17(decoder_1_out16), .in18(decoder_1_out26), .in19(decoder_1_out24),
    .in20(decoder_1_out30), .in21(decoder_1_out28), .in22(decoder_2_out0), .in23(decoder_2_out1),
    .in24(decoder_2_out2), .in25(decoder_2_out3), .in26(decoder_2_out4), .in27(decoder_2_out5),
    .in28(decoder_2_out6), .in29(decoder_2_out7), .out(ALUCmd_sel), .gs(priority_encoder_2_gs), .en_in(1'b1));  // open: in0, in30, in31, en_out

  // Notes on the sheet:
  //   Br
  //   JALR
  //   JAL
  //   JALR
  //   b30
  //   5 auipc
  //   4 Lui
  //   23 MULH
  //   26 DIV
  //   28 REM
  //   17 XORI
  //   13 SRLI
  //   15 SRAI
  //   22 MUL
  //   24 MULHSU
  //   25 MULHU
  //   27 DIVU
  //   29 REMU
  //   10 SLL
  //   9 SLTIU
  //   16 XOR
  //   2 Addi
  //   1 Add
  //   3 Sub
  //   7 SLTI
  //   6 SLT
  //   8 SLTU
  //   12 SRL
  //   14 SRA
  //   18 OR
  //   20 AND
  //   21 ANDI
  //   11 SLLI
  //   19 ORI
endmodule

module Imm_Gen (
  input  [31:0] Instruction,
  output [31:0] Imm_out,
  output [31:0] BrOffset,
  output [31:0] jalOffset,
  output [31:0] uiOffset
);

  wire [31:0] bit_extender_2_out, bit_extender_3_out, bit_extender_4_out;

  assign Imm_out = {{20{Instruction[31]}}, Instruction[31:20]};  // Bit_Extender bit_extender_1
  assign bit_extender_2_out = {{12{Instruction[31]}}, {Instruction[31], Instruction[19:12], Instruction[20], Instruction[30:21]}};  // Bit_Extender bit_extender_2
  assign bit_extender_3_out = {{12{Instruction[31]}}, Instruction[31:12]};  // Bit_Extender bit_extender_3
  assign bit_extender_4_out = {{20{Instruction[31]}}, {Instruction[31], Instruction[7], Instruction[30:25], Instruction[11:8]}};  // Bit_Extender bit_extender_4
  Shifter #(.width(32)) shifter_1 (.in(bit_extender_3_out), .\dist (5'b01100), .out(uiOffset));
  Shifter #(.width(32)) shifter_2 (.in(bit_extender_4_out), .\dist (5'b00001), .out(BrOffset));
  Shifter #(.width(32)) shifter_3 (.in(bit_extender_2_out), .\dist (5'b00001), .out(jalOffset));
endmodule

module Reg_File (
  input  [4:0] Rs1,
  input  [4:0] Rs2,
  input  [31:0] WData,
  input  [4:0] Rd,
  input  RegW_En,
  input  Clear,
  output [31:0] Rs1Data,
  output [31:0] Rs2Data
);

  wire clock_1_out, decoder_1_out0, decoder_1_out1, decoder_2_out0, decoder_2_out1, decoder_2_out2,
       decoder_2_out3, decoder_3_out0, decoder_3_out1, decoder_3_out2, decoder_3_out3, decoder_4_out0,
       decoder_4_out1, decoder_4_out2, decoder_4_out3, decoder_5_out0, decoder_5_out1, decoder_5_out2,
       decoder_5_out3, decoder_6_out0, decoder_6_out1, decoder_6_out2, decoder_6_out3, decoder_7_out0,
       decoder_7_out1, decoder_7_out2, decoder_7_out3, decoder_8_out0, decoder_8_out1, decoder_8_out2,
       decoder_8_out3, decoder_9_out0, decoder_9_out1, decoder_9_out2, decoder_9_out3, decoder_10_out0,
       decoder_10_out1, decoder_10_out2, decoder_10_out3, decoder_11_out0, decoder_11_out1, decoder_11_out2,
       decoder_11_out3;
  wire [31:0] multiplexer_1_out, multiplexer_2_out, multiplexer_3_out, multiplexer_4_out, multiplexer_5_out,
       multiplexer_6_out, multiplexer_7_out, multiplexer_8_out, multiplexer_9_out, multiplexer_10_out,
       multiplexer_13_out, multiplexer_14_out, multiplexer_15_out, multiplexer_16_out, multiplexer_17_out,
       multiplexer_18_out, multiplexer_19_out, multiplexer_20_out, multiplexer_21_out, multiplexer_22_out,
       x0_q, x1_q, x2_q, x3_q, x4_q, x5_q, x6_q, x7_q, x8_q, x9_q, x10_q, x11_q, x12_q, x13_q, x14_q, x15_q,
       x16_q, x17_q, x18_q, x19_q, x20_q, x21_q, x22_q, x23_q, x24_q, x25_q, x26_q, x27_q, x28_q, x29_q,
       x30_q, x31_q;

  Decoder #(.disabled(0)) decoder_1 (.out0(decoder_1_out0), .out1(decoder_1_out1), .sel(Rd[4]), .en(RegW_En));
  Clock clock_1 (.out(clock_1_out));
  Decoder #(.select(2), .disabled(0)) decoder_2 (
    .out0(decoder_2_out0), .out1(decoder_2_out1), .out2(decoder_2_out2), .out3(decoder_2_out3),
    .sel(Rd[3:2]), .en(decoder_1_out0));
  Decoder #(.select(2), .disabled(0)) decoder_3 (
    .out0(decoder_3_out0), .out1(decoder_3_out1), .out2(decoder_3_out2), .out3(decoder_3_out3),
    .sel(Rd[1:0]), .en(decoder_2_out0));
  Decoder #(.select(2), .disabled(0)) decoder_4 (
    .out0(decoder_4_out0), .out1(decoder_4_out1), .out2(decoder_4_out2), .out3(decoder_4_out3),
    .sel(Rd[1:0]), .en(decoder_2_out1));
  Decoder #(.select(2), .disabled(0)) decoder_5 (
    .out0(decoder_5_out0), .out1(decoder_5_out1), .out2(decoder_5_out2), .out3(decoder_5_out3),
    .sel(Rd[1:0]), .en(decoder_2_out2));
  Decoder #(.select(2), .disabled(0)) decoder_6 (
    .out0(decoder_6_out0), .out1(decoder_6_out1), .out2(decoder_6_out2), .out3(decoder_6_out3),
    .sel(Rd[1:0]), .en(decoder_2_out3));
  Register #(.width(32)) x0 (.D({32{1'b0}}), .en(decoder_3_out0), .Q(x0_q), .clk(clock_1_out), .clr(Clear));
  Register #(.width(32)) x1 (.D(WData), .en(decoder_3_out1), .Q(x1_q), .clk(clock_1_out), .clr(Clear));
  Register #(.width(32)) x2 (.D(WData), .en(decoder_3_out2), .Q(x2_q), .clk(clock_1_out), .clr(Clear));
  Register #(.width(32)) x3 (.D(WData), .en(decoder_3_out3), .Q(x3_q), .clk(clock_1_out), .clr(Clear));
  Register #(.width(32)) x4 (.D(WData), .en(decoder_4_out0), .Q(x4_q), .clk(clock_1_out), .clr(Clear));
  Register #(.width(32)) x5 (.D(WData), .en(decoder_4_out1), .Q(x5_q), .clk(clock_1_out), .clr(Clear));
  Register #(.width(32)) x6 (.D(WData), .en(decoder_4_out2), .Q(x6_q), .clk(clock_1_out), .clr(Clear));
  Register #(.width(32)) x7 (.D(WData), .en(decoder_4_out3), .Q(x7_q), .clk(clock_1_out), .clr(Clear));
  Register #(.width(32)) x8 (.D(WData), .en(decoder_5_out0), .Q(x8_q), .clk(clock_1_out), .clr(Clear));
  Register #(.width(32)) x9 (.D(WData), .en(decoder_5_out1), .Q(x9_q), .clk(clock_1_out), .clr(Clear));
  Register #(.width(32)) x10 (.D(WData), .en(decoder_5_out2), .Q(x10_q), .clk(clock_1_out), .clr(Clear));
  Register #(.width(32)) x11 (.D(WData), .en(decoder_5_out3), .Q(x11_q), .clk(clock_1_out), .clr(Clear));
  Register #(.width(32)) x12 (.D(WData), .en(decoder_6_out0), .Q(x12_q), .clk(clock_1_out), .clr(Clear));
  Register #(.width(32)) x13 (.D(WData), .en(decoder_6_out1), .Q(x13_q), .clk(clock_1_out), .clr(Clear));
  Register #(.width(32)) x14 (.D(WData), .en(decoder_6_out2), .Q(x14_q), .clk(clock_1_out), .clr(Clear));
  Register #(.width(32)) x15 (.D(WData), .en(decoder_6_out3), .Q(x15_q), .clk(clock_1_out), .clr(Clear));
  Multiplexer #(.select(2), .width(32), .disabled(0)) multiplexer_1 (
    .in0(x0_q), .in1(x1_q), .in2(x2_q), .in3(x3_q), .out(multiplexer_1_out), .sel(Rs1[1:0]), .en(1'b1));
  Multiplexer #(.select(2), .width(32), .disabled(0)) multiplexer_2 (
    .in0(x4_q), .in1(x5_q), .in2(x6_q), .in3(x7_q), .out(multiplexer_2_out), .sel(Rs1[1:0]), .en(1'b1));
  Multiplexer #(.select(2), .width(32), .disabled(0)) multiplexer_3 (
    .in0(x8_q), .in1(x9_q), .in2(x10_q), .in3(x11_q), .out(multiplexer_3_out), .sel(Rs1[1:0]), .en(1'b1));
  Multiplexer #(.select(2), .width(32), .disabled(0)) multiplexer_4 (
    .in0(x12_q), .in1(x13_q), .in2(x14_q), .in3(x15_q), .out(multiplexer_4_out), .sel(Rs1[1:0]), .en(1'b1));
  Multiplexer #(.select(2), .width(32), .disabled(0)) multiplexer_5 (
    .in0(x0_q), .in1(x1_q), .in2(x2_q), .in3(x3_q), .out(multiplexer_5_out), .sel(Rs2[1:0]), .en(1'b1));
  Multiplexer #(.select(2), .width(32), .disabled(0)) multiplexer_6 (
    .in0(x4_q), .in1(x5_q), .in2(x6_q), .in3(x7_q), .out(multiplexer_6_out), .sel(Rs2[1:0]), .en(1'b1));
  Multiplexer #(.select(2), .width(32), .disabled(0)) multiplexer_7 (
    .in0(x8_q), .in1(x9_q), .in2(x10_q), .in3(x11_q), .out(multiplexer_7_out), .sel(Rs2[1:0]), .en(1'b1));
  Multiplexer #(.select(2), .width(32), .disabled(0)) multiplexer_8 (
    .in0(x12_q), .in1(x13_q), .in2(x14_q), .in3(x15_q), .out(multiplexer_8_out), .sel(Rs2[1:0]), .en(1'b1));
  Multiplexer #(.select(2), .width(32), .disabled(0)) multiplexer_9 (
    .in0(multiplexer_1_out), .in1(multiplexer_2_out), .in2(multiplexer_3_out), .in3(multiplexer_4_out),
    .out(multiplexer_9_out), .sel(Rs1[3:2]), .en(1'b1));
  Multiplexer #(.select(2), .width(32), .disabled(0)) multiplexer_10 (
    .in0(multiplexer_5_out), .in1(multiplexer_6_out), .in2(multiplexer_7_out), .in3(multiplexer_8_out),
    .out(multiplexer_10_out), .sel(Rs2[3:2]), .en(1'b1));
  Decoder #(.select(2), .disabled(0)) decoder_7 (
    .out0(decoder_7_out0), .out1(decoder_7_out1), .out2(decoder_7_out2), .out3(decoder_7_out3),
    .sel(Rd[3:2]), .en(decoder_1_out1));
  Multiplexer #(.width(32), .disabled(0)) multiplexer_11 (
    .in0(multiplexer_9_out), .in1(multiplexer_21_out), .out(Rs1Data), .sel(Rs1[4]), .en(1'b1));
  Multiplexer #(.width(32), .disabled(0)) multiplexer_12 (
    .in0(multiplexer_10_out), .in1(multiplexer_22_out), .out(Rs2Data), .sel(Rs2[4]), .en(1'b1));
  Decoder #(.select(2), .disabled(0)) decoder_8 (
    .out0(decoder_8_out0), .out1(decoder_8_out1), .out2(decoder_8_out2), .out3(decoder_8_out3),
    .sel(Rd[1:0]), .en(decoder_7_out0));
  Decoder #(.select(2), .disabled(0)) decoder_9 (
    .out0(decoder_9_out0), .out1(decoder_9_out1), .out2(decoder_9_out2), .out3(decoder_9_out3),
    .sel(Rd[1:0]), .en(decoder_7_out1));
  Decoder #(.select(2), .disabled(0)) decoder_10 (
    .out0(decoder_10_out0), .out1(decoder_10_out1), .out2(decoder_10_out2), .out3(decoder_10_out3),
    .sel(Rd[1:0]), .en(decoder_7_out2));
  Decoder #(.select(2), .disabled(0)) decoder_11 (
    .out0(decoder_11_out0), .out1(decoder_11_out1), .out2(decoder_11_out2), .out3(decoder_11_out3),
    .sel(Rd[1:0]), .en(decoder_7_out3));
  Register #(.width(32)) x16 (.D(WData), .en(decoder_8_out0), .Q(x16_q), .clk(clock_1_out), .clr(Clear));
  Register #(.width(32)) x17 (.D(WData), .en(decoder_8_out1), .Q(x17_q), .clk(clock_1_out), .clr(Clear));
  Register #(.width(32)) x18 (.D(WData), .en(decoder_8_out2), .Q(x18_q), .clk(clock_1_out), .clr(Clear));
  Register #(.width(32)) x19 (.D(WData), .en(decoder_8_out3), .Q(x19_q), .clk(clock_1_out), .clr(Clear));
  Register #(.width(32)) x20 (.D(WData), .en(decoder_9_out0), .Q(x20_q), .clk(clock_1_out), .clr(Clear));
  Register #(.width(32)) x21 (.D(WData), .en(decoder_9_out1), .Q(x21_q), .clk(clock_1_out), .clr(Clear));
  Register #(.width(32)) x22 (.D(WData), .en(decoder_9_out2), .Q(x22_q), .clk(clock_1_out), .clr(Clear));
  Register #(.width(32)) x23 (.D(WData), .en(decoder_9_out3), .Q(x23_q), .clk(clock_1_out), .clr(Clear));
  Register #(.width(32)) x24 (.D(WData), .en(decoder_10_out0), .Q(x24_q), .clk(clock_1_out), .clr(Clear));
  Register #(.width(32)) x25 (.D(WData), .en(decoder_10_out1), .Q(x25_q), .clk(clock_1_out), .clr(Clear));
  Register #(.width(32)) x26 (.D(WData), .en(decoder_10_out2), .Q(x26_q), .clk(clock_1_out), .clr(Clear));
  Register #(.width(32)) x27 (.D(WData), .en(decoder_10_out3), .Q(x27_q), .clk(clock_1_out), .clr(Clear));
  Register #(.width(32)) x28 (.D(WData), .en(decoder_11_out0), .Q(x28_q), .clk(clock_1_out), .clr(Clear));
  Register #(.width(32)) x29 (.D(WData), .en(decoder_11_out1), .Q(x29_q), .clk(clock_1_out), .clr(Clear));
  Register #(.width(32)) x30 (.D(WData), .en(decoder_11_out2), .Q(x30_q), .clk(clock_1_out), .clr(Clear));
  Register #(.width(32)) x31 (.D(WData), .en(decoder_11_out3), .Q(x31_q), .clk(clock_1_out), .clr(Clear));
  Register #(.width(32)) register_1 (.clk(clock_1_out));  // open: D, en, Q, clr
  Register #(.width(32)) register_2 (.clk(clock_1_out));  // open: D, en, Q, clr
  Multiplexer #(.select(2), .width(32), .disabled(0)) multiplexer_13 (
    .in0(x16_q), .in1(x17_q), .in2(x18_q), .in3(x19_q), .out(multiplexer_13_out), .sel(Rs1[1:0]), .en(1'b1));
  Multiplexer #(.select(2), .width(32), .disabled(0)) multiplexer_14 (
    .in0(x20_q), .in1(x21_q), .in2(x22_q), .in3(x23_q), .out(multiplexer_14_out), .sel(Rs1[1:0]), .en(1'b1));
  Multiplexer #(.select(2), .width(32), .disabled(0)) multiplexer_15 (
    .in0(x24_q), .in1(x25_q), .in2(x26_q), .in3(x27_q), .out(multiplexer_15_out), .sel(Rs1[1:0]), .en(1'b1));
  Multiplexer #(.select(2), .width(32), .disabled(0)) multiplexer_16 (
    .in0(x28_q), .in1(x29_q), .in2(x30_q), .in3(x31_q), .out(multiplexer_16_out), .sel(Rs1[1:0]), .en(1'b1));
  Multiplexer #(.select(2), .width(32), .disabled(0)) multiplexer_17 (
    .in0(x16_q), .in1(x17_q), .in2(x18_q), .in3(x19_q), .out(multiplexer_17_out), .sel(Rs2[1:0]), .en(1'b1));
  Multiplexer #(.select(2), .width(32), .disabled(0)) multiplexer_18 (
    .in0(x20_q), .in1(x21_q), .in2(x22_q), .in3(x23_q), .out(multiplexer_18_out), .sel(Rs2[1:0]), .en(1'b1));
  Multiplexer #(.select(2), .width(32), .disabled(0)) multiplexer_19 (
    .in0(x24_q), .in1(x25_q), .in2(x26_q), .in3(x27_q), .out(multiplexer_19_out), .sel(Rs2[1:0]), .en(1'b1));
  Multiplexer #(.select(2), .width(32), .disabled(0)) multiplexer_20 (
    .in0(x28_q), .in1(x29_q), .in2(x30_q), .in3(x31_q), .out(multiplexer_20_out), .sel(Rs2[1:0]), .en(1'b1));
  Multiplexer #(.select(2), .width(32)) multiplexer_21 (
    .in0(multiplexer_13_out), .in1(multiplexer_14_out), .in2(multiplexer_15_out), .in3(multiplexer_16_out),
    .out(multiplexer_21_out), .sel(Rs1[3:2]), .en(1'b1));
  Multiplexer #(.select(2), .width(32)) multiplexer_22 (
    .in0(multiplexer_17_out), .in1(multiplexer_18_out), .in2(multiplexer_19_out), .in3(multiplexer_20_out),
    .out(multiplexer_22_out), .sel(Rs2[3:2]), .en(1'b1));

  // Notes on the sheet:
  //   for Reg 1
  //   for Reg 2
  //   for Reg 1
  //   for Reg 2
endmodule

module ALU (
  input  [31:0] PC,
  input  [31:0] uiOffset,
  input  [31:0] A,
  input  ALU_sel,
  input  [31:0] B,
  input  [4:0] ALUCmd_sel,
  output [31:0] ALU_out
);

  wire comparator_1_lt, comparator_2_lt, comparator_3_lt, comparator_4_lt;
  wire [4:0] bit_extender_1_out, bit_extender_2_out, bit_extender_3_out, bit_extender_4_out,
       bit_extender_5_out, bit_extender_6_out;
  wire [31:0] adder_1_out, adder_2_out, adder_3_out, adder_4_out, and_1_out, and_2_out, bit_extender_7_out,
       bit_extender_8_out, bit_extender_9_out, bit_extender_10_out, divider_2_out, divider_4_rem,
       multiplier_1_out, multiplier_2_out, negator_1_out, or_1_out, or_2_out, shifter_1_out, shifter_2_out,
       shifter_3_out, shifter_4_out, shifter_5_out, shifter_6_out, undriven, undriven_2, undriven_3,
       undriven_4, undriven_5, undriven_6, undriven_7, XOR_2_out, XOR_out;

  Negator #(.width(32)) negator_1 (.in(B), .out(negator_1_out));
  Comparator #(.width(32)) comparator_1 (.a(A), .b(B), .lt(comparator_1_lt));  // open: gt, eq
  Comparator #(.width(32)) comparator_2 (.a(A), .b(B), .lt(comparator_2_lt));  // open: gt, eq
  Comparator #(.width(32), .mode("unsigned")) comparator_3 (.a(A), .b(B), .lt(comparator_3_lt));  // open: gt, eq
  Comparator #(.width(32), .mode("unsigned")) comparator_4 (.a(A), .b(B), .lt(comparator_4_lt));  // open: gt, eq
  Bit_Extender #(.in_width(32), .out_width(5)) bit_extender_1 (.in(B), .out(bit_extender_1_out));
  Bit_Extender #(.in_width(32), .out_width(5)) bit_extender_2 (.in(B), .out(bit_extender_2_out));
  Bit_Extender #(.in_width(32), .out_width(5)) bit_extender_3 (.in(B), .out(bit_extender_3_out));
  Bit_Extender #(.in_width(32), .out_width(5)) bit_extender_4 (.in(B), .out(bit_extender_4_out));
  Bit_Extender #(.in_width(32), .out_width(5)) bit_extender_5 (.in(B), .out(bit_extender_5_out));
  Bit_Extender #(.in_width(32), .out_width(5)) bit_extender_6 (.in(B), .out(bit_extender_6_out));
  assign XOR_out = A ^ B;  // XOR_Gate XOR, 32 bits wide
  assign XOR_2_out = A ^ B;  // XOR_Gate XOR_2, 32 bits wide
  assign or_1_out = A | B;  // OR_Gate or_1, 32 bits wide
  assign or_2_out = A | B;  // OR_Gate or_2, 32 bits wide
  assign and_1_out = A & B;  // AND_Gate and_1, 32 bits wide
  assign and_2_out = A & B;  // AND_Gate and_2, 32 bits wide
  Adder #(.width(32)) adder_1 (.a(A), .b(B), .out(adder_1_out));  // open: cin, cout
  Adder #(.width(32)) adder_2 (.a(A), .b(B), .out(adder_2_out));  // open: cin, cout
  Adder #(.width(32)) adder_3 (.a(A), .b(negator_1_out), .out(adder_3_out));  // open: cin, cout
  Adder #(.width(32)) adder_4 (.a(PC), .b(uiOffset), .out(adder_4_out));  // open: cin, cout
  assign bit_extender_7_out = {{31{1'b0}}, comparator_1_lt};  // Bit_Extender bit_extender_7
  assign bit_extender_8_out = {{31{1'b0}}, comparator_2_lt};  // Bit_Extender bit_extender_8
  assign bit_extender_9_out = {{31{1'b0}}, comparator_3_lt};  // Bit_Extender bit_extender_9
  assign bit_extender_10_out = {{31{1'b0}}, comparator_4_lt};  // Bit_Extender bit_extender_10
  Shifter #(.width(32)) shifter_1 (.in(A), .\dist (bit_extender_1_out), .out(shifter_1_out));
  Shifter #(.width(32)) shifter_2 (.in(A), .\dist (bit_extender_2_out), .out(shifter_2_out));
  Shifter #(.width(32), .shift("lr")) shifter_3 (.in(A), .\dist (bit_extender_3_out), .out(shifter_3_out));
  Shifter #(.width(32), .shift("lr")) shifter_4 (.in(A), .\dist (bit_extender_4_out), .out(shifter_4_out));
  Shifter #(.width(32), .shift("ar")) shifter_5 (.in(A), .\dist (bit_extender_5_out), .out(shifter_5_out));
  Shifter #(.width(32), .shift("ar")) shifter_6 (.in(A), .\dist (bit_extender_6_out), .out(shifter_6_out));
  Multiplier #(.width(32)) multiplier_1 (.a(A), .b(B), .out(multiplier_1_out));  // open: cin, cout
  Multiplier #(.width(32)) multiplier_2 (.out(multiplier_2_out));  // open: a, b, cin, cout
  Shifter #(.width(32), .shift("lr")) shifter_7 (.in(multiplier_2_out), .\dist ({5{1'b0}}));  // open: out
  Multiplier #(.width(32)) multiplier_3 ();  // open: a, b, out, cin, cout
  Multiplier #(.width(32)) multiplier_4 ();  // open: a, b, out, cin, cout
  Divider #(.width(32)) divider_1 (.a(undriven), .b(undriven_2));  // open: out, upper, rem
  Divider #(.width(32)) divider_2 (.a(A), .b(B), .out(divider_2_out));  // open: upper, rem
  Divider #(.width(32)) divider_3 ();  // open: a, b, out, upper, rem
  Divider #(.width(32)) divider_4 (.a(A), .b(B), .rem(divider_4_rem));  // open: out, upper
  Multiplexer #(.select(5), .width(32)) multiplexer_1 (
    .in1(adder_1_out), .in2(adder_2_out), .in3(adder_3_out), .in4(uiOffset), .in5(adder_4_out),
    .in6(bit_extender_7_out), .in7(bit_extender_8_out), .in8(bit_extender_9_out), .in9(bit_extender_10_out),
    .in10(shifter_1_out), .in11(shifter_2_out), .in12(shifter_3_out), .in13(shifter_4_out),
    .in14(shifter_5_out), .in15(shifter_6_out), .in16(XOR_out), .in17(XOR_2_out), .in18(or_1_out),
    .in19(or_2_out), .in20(and_1_out), .in21(and_2_out), .in22(multiplier_1_out), .in23(undriven_4),
    .in24(undriven_5), .in25(undriven_6), .in26(undriven_7), .in27(divider_2_out), .in28(undriven_3),
    .in29(divider_4_rem), .out(ALU_out), .sel(ALUCmd_sel), .en(ALU_sel));  // open: in0, in30, in31

  // Notes on the sheet:
  //   B
  //   A
  //   B
  //   6 SLT
  //   7 SLTI
  //   16 XOR
  //   17 XORI
  //   18 OR
  //   19 ORI
  //   20 AND
  //   21 ANDI
  //   22 MUL
  //   24 MULHU
  //   25 MULHSU
  //   27 DIVU
  //   28 REM
  //   29 REMU
  //   1 Add
  //   2 Addi
  //   3 Sub
  //   4 Lui
  //   5 Auipc
  //   8 SLTU
  //   9 SLTIU
  //   10 SLL
  //   11 SLLI
  //   12 SRL
  //   13 SRLI
  //   14 SRA
  //   15 SRAI
  //   23 MULH
  //   26 DIV
  //   Multiplier is doing signed multiplication
  //   and giving lower 32-bits at the output.
  //   Divider is doing unsigned division.
  //   Divider is doing unsigned division.
endmodule

module DMEM (
  input  Address,
  input  Write_Data,
  output Read_Data
);
endmodule
